# Fritzing sketch kropp (saved by Fritzing 0.9.3b)
circuit board: 6.69996cm x 9.58027cm
circuit board: 6.69996cm x 9.58027cm
circuit board: 6.69996cm x 9.58027cm
circuit board: 6.69996cm x 9.58027cm
breadboards: 1

parts:
  J21 = female pin header, 1 pin [form="♀ (female)"]
  J22 = female pin header, 1 pin [form="♀ (female)"]
  J23 = female pin header, 1 pin [form="♀ (female)"]
  J24 = female pin header, 1 pin [form="♀ (female)"]
  J26 = female pin header, 1 pin [form="♀ (female)"]
  J27 = female pin header, 1 pin [form="♀ (female)"]
  J28 = female pin header, 1 pin [form="♀ (female)"]
  J30 = female pin header, 1 pin [form="♀ (female)"]
  J31 = female pin header, 1 pin [form="♀ (female)"]
  J32 = female pin header, 1 pin [form="♀ (female)"]
  J33 = female pin header, 1 pin [form="♀ (female)"]
  J34 = female pin header, 1 pin [form="♀ (female)"]
  J35 = female pin header, 1 pin [form="♀ (female)"]
  J36 = female pin header, 1 pin [form="♀ (female)"]
  J37 = female pin header, 1 pin [form="♀ (female)"]
  Part1 = Arduino Micro (Rev3)
  J38 = female pin header, 1 pin [form="♀ (female)"]
  J39 = female pin header, 1 pin [form="♀ (female)"]
  J40 = female pin header, 1 pin [form="♀ (female)"]
  J41 = female pin header, 1 pin [form="♀ (female)"]
  J42 = female pin header, 1 pin [form="♀ (female)"]
  J43 = female pin header, 1 pin [form="♀ (female)"]
  J44 = female pin header, 1 pin [form="♀ (female)"]
  J45 = female pin header, 1 pin [form="♀ (female)"]
  J46 = female pin header, 1 pin [form="♀ (female)"]
  J47 = female pin header, 1 pin [form="♀ (female)"]
  J48 = female pin header, 1 pin [form="♀ (female)"]
  J49 = female pin header, 1 pin [form="♀ (female)"]
  J50 = female pin header, 1 pin [form="♀ (female)"]
  J51 = female pin header, 1 pin [form="♀ (female)"]
  J52 = female pin header, 1 pin [form="♀ (female)"]
  J53 = female pin header, 1 pin [form="♀ (female)"]
  J54 = female pin header, 1 pin [form="♀ (female)"]
  J55 = female pin header, 2 pins [form="♀ (female)"]
  J56 = female pin header, 3 pins [form="♀ (female)"]
  J67 = female pin header, 1 pin [form="♀ (female)"]  # not connected
  J68 = female pin header, 1 pin [form="♀ (female)"]  # not connected
  J69 = female pin header, 1 pin [form="♀ (female)"]  # not connected
  J70 = female pin header, 1 pin [form="♀ (female)"]  # not connected
  J71 = female pin header, 1 pin [form="♀ (female)"]  # not connected
  J72 = female pin header, 1 pin [form="♀ (female)"]  # not connected
  J73 = female pin header, 1 pin [form="♀ (female)"]  # not connected
  J74 = female pin header, 1 pin [form="♀ (female)"]  # not connected
  J75 = female pin header, 1 pin [form="♀ (female)"]  # not connected
  J76 = female pin header, 1 pin [form="♀ (female)"]  # not connected
  J77 = female pin header, 1 pin [form="♀ (female)"]  # not connected
  J78 = female pin header, 1 pin [form="♀ (female)"]  # not connected
  J79 = female pin header, 1 pin [form="♀ (female)"]  # not connected
  J80 = female pin header, 1 pin [form="♀ (female)"]  # not connected
  J81 = female pin header, 1 pin [form="♀ (female)"]  # not connected
  J82 = female pin header, 1 pin [form="♀ (female)"]  # not connected
  J83 = female pin header, 1 pin [form="♀ (female)"]  # not connected
  J84 = female pin header, 1 pin [form="♀ (female)"]  # not connected
  J85 = female pin header, 1 pin [form="♀ (female)"]  # not connected
  J86 = female pin header, 1 pin [form="♀ (female)"]  # not connected
  J87 = female pin header, 1 pin [form="♀ (female)"]  # not connected
  J88 = female pin header, 1 pin [form="♀ (female)"]  # not connected
  J89 = female pin header, 1 pin [form="♀ (female)"]  # not connected
  J90 = female pin header, 1 pin [form="♀ (female)"]  # not connected

nets:
  N1: J21.pin1, Part1.SCK
  N2: J22.pin1, Part1.MISO
  N3: J23.pin1, Part1.VIN
  N4: J24.pin1, Part1.A5
  N5: J26.pin1, Part1.GND, J45.pin1, J55.pin2, J56.pin3
  N6: J27.pin1, Part1.RESET, J40.pin1
  N7: J28.pin1, Part1.5V, J56.pin2
  N8: J30.pin1, Part1.A2
  N9: J31.pin1, Part1.A3
  N10: J32.pin1, Part1.AREF
  N11: J33.pin1, Part1.3V3
  N12: J34.pin1, Part1.D13_PWM, J55.pin1
  N13: J35.pin1, Part1.A4
  N14: J36.pin1, Part1.A1
  N15: J37.pin1, Part1.A0
  N16: Part1.MOSI, J49.pin1
  N17: Part1.RXLED/SS, J38.pin1
  N18: Part1.D1/TX, J51.pin1
  N19: Part1.D0/RX, J47.pin1
  N20: Part1.D2/SDA, J52.pin1
  N21: Part1.D3/SCL, J39.pin1
  N22: Part1.D4_PWM/A6, J41.pin1
  N23: Part1.D5_PWM, J53.pin1
  N24: Part1.D6_PWM/A7, J44.pin1
  N25: Part1.D7, J50.pin1
  N26: Part1.D8_PWM/A8, J54.pin1
  N27: Part1.D9_PWM/A9, J46.pin1, J56.pin1
  N28: Part1.D10_PWM/A10, J48.pin1
  N29: Part1.D11_PWM, J43.pin1
  N30: Part1.D12_PWM/A11, J42.pin1
